# Fritzing sketch LED-pot-sw (saved by Fritzing 0.9.9b)
breadboards: 1

parts:
  Part1 = Arduino Leonardo (Rev3b)
  LED1 = LED - 5mm [color="Red (633nm)" current=0.030 package="5 mm [THT]"]
  POT1 = Breadboard Trimpot
  S2 = Pushbutton [package="[SMD]"]
  R1 = Resistor [tolerance=±5% power=0.25 resistance=220 package=THT]

nets:
  N1: Part1.D2/SDA, Part1.SDA, S2.Pin_3, S2.Pin_4
  N2: Part1.5V, POT1.PIN1
  N3: Part1.GND, LED1.cathode, POT1.PIN3, S2.Pin_1, S2.Pin_2
  N4: Part1.A0, POT1.PIN2
  N5: Part1.D12/A11, R1.Pin_0
  N6: LED1.anode, R1.Pin_1
