# Fritzing sketch LED (saved by Fritzing 0.9.9b)
breadboards: 1

parts:
  Part1 = Arduino Leonardo (Rev3b)
  LED1 = LED - 5mm [color="Red (633nm)" current=0.030 package="5 mm [THT]"]
  R1 = Resistor [tolerance=±5% power=0.25 resistance=220 package=THT]

nets:
  N1: Part1.GND, LED1.cathode
  N2: Part1.D13_PWM, R1.Pin_0
  N3: LED1.anode, R1.Pin_1
