# Fritzing sketch neopixel-chain (saved by Fritzing 0.9.9b)
breadboards: 1

parts:
  Part1 = Arduino Leonardo (Rev3b)
  Part2 = NeoPixel Stick [part_number=1426]
  R1 = Resistor [tolerance=±1% power=0.25 resistance=470 package=THT]
  Part3 = NeoPixel Stick [part_number=1426]

nets:
  N1: Part1.D6_PWM/A7, R1.Pin_0
  +5V: Part2.+5V, Part3.+5V
  N2: Part2.DATAIN, Part3.DATAOUT
  GND: Part2.GND, Part3.GND

custom parts:
  NeoPixel Stick: Make your own little LED strip arrangement with this stick of NeoPixel LEDs. We crammed 8 of the tiny 5050 (5mm x 5mm) smart RGB LEDs onto a PCB with mounting holes and a chainable design. Use only one microcontroller pin to control as many as you can chain together! Each LED is addressable as the driver chip is inside the LED. Each one has ~18mA constant current drive so the color will be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
