# Fritzing sketch din-midi (saved by Fritzing 1.0.5)
breadboards: 1

parts:
  IC1 = IC, DIP package, 14 pins [chip_label=74LS04]
  R1 = Resistor [tolerance=±5% resistance=220 package="2512 [SMD]"]
  DIN1 = DIN-5 jack (MIDI) [package=THT]
  Part2 = Arduino Leonardo (Rev3b)
  R2 = Resistor [tolerance=±5% resistance=220 package="2512 [SMD]"]

nets:
  N1: IC1.pin7, DIN1.2, Part2.GND
  N2: IC1.pin10, R1.Pin_0
  N3: IC1.pin11, IC1.pin12
  N4: IC1.pin13, Part2.D1/TX
  N5: IC1.pin14, Part2.5V, R2.Pin_0
  N6: R1.Pin_1, DIN1.5
  N7: DIN1.4, R2.Pin_1
