# Fritzing sketch switch-pot (saved by Fritzing 0.9.9b)
breadboards: 1

parts:
  Part1 = Arduino Leonardo (Rev3b)
  S2 = Pushbutton [package="[SMD]"]
  POT1 = Breadboard Trimpot

nets:
  N1: Part1.D2/SDA, S2.Pin_3, S2.Pin_4
  N2: Part1.5V, POT1.PIN1
  N3: Part1.GND, S2.Pin_1, S2.Pin_2, POT1.PIN3
  N4: Part1.A0, POT1.PIN2
