# Fritzing sketch switch-switch-pot-neopixel (saved by Fritzing 0.9.9b)
breadboards: 1

parts:
  Part1 = Arduino Leonardo (Rev3b)
  S2 = Pushbutton [package="[SMD]"]
  POT1 = Breadboard Trimpot
  S3 = Pushbutton [package="[SMD]"]
  Part2 = NeoPixel Stick [part_number=1426]

nets:
  N1: Part1.D2/SDA, S2.Pin_3, S2.Pin_4
  N2: Part1.D3_PWM/SCL, Part1.SCL, S3.Pin_3, S3.Pin_4
  5V: Part1.5V, POT1.PIN1, Part2.+5V
  GND: Part1.GND, S2.Pin_1, S2.Pin_2, POT1.PIN3, S3.Pin_1, S3.Pin_2, Part2.GND
  N3: Part1.A0, POT1.PIN2

custom parts:
  NeoPixel Stick: Make your own little LED strip arrangement with this stick of NeoPixel LEDs. We crammed 8 of the tiny 5050 (5mm x 5mm) smart RGB LEDs onto a PCB with mounting holes and a chainable design. Use only one microcontroller pin to control as many as you can chain together! Each LED is addressable as the driver chip is inside the LED. Each one has ~18mA constant current drive so the color will be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
