# Fritzing sketch switch (saved by Fritzing 0.9.9b)
breadboards: 1

parts:
  Part1 = Arduino Leonardo (Rev3b)
  S2 = Pushbutton [package="[SMD]"]

nets:
  N1: Part1.D2/SDA, S2.Pin_3, S2.Pin_4
  N2: Part1.GND, S2.Pin_1, S2.Pin_2
