# Fritzing sketch switch-pot-ldr-mpu6050 (saved by Fritzing 0.9.9b)
breadboards: 1

parts:
  Part1 = Arduino Leonardo (Rev3b)
  S2 = Pushbutton [package="[SMD]"]
  POT1 = Breadboard Trimpot
  R1 = Photocell (LDR) [package=THT]
  R2 = Resistor [tolerance=±5% power=0.25 resistance=10k package=THT]
  Part2 = InvenSense MPU6050

nets:
  N1: Part1.D2/SDA, Part2.SDA
  N2: Part1.D3_PWM/SCL, Part2.SCL
  N3: Part1.D4/A6, S2.Pin_3, S2.Pin_4
  5V: Part1.5V, POT1.PIN1, R1.pin_0, Part2.VCC
  GND: Part1.GND, S2.Pin_1, S2.Pin_2, POT1.PIN3, R2.Pin_1, Part2.GND
  N4: Part1.A0, POT1.PIN2
  N5: Part1.A1, R1.pin_1, R2.Pin_0
