# Fritzing sketch switch-pot-ldr (saved by Fritzing 0.9.9b)
breadboards: 1

parts:
  Part1 = Arduino Leonardo (Rev3b)
  S2 = Pushbutton [package="[SMD]"]
  POT1 = Breadboard Trimpot
  R1 = Photocell (LDR) [package=THT]
  R2 = Resistor [tolerance=±5% power=0.25 resistance=10k package=THT]

nets:
  N1: Part1.D2/SDA, Part1.SDA, S2.Pin_3, S2.Pin_4
  N2: Part1.5V, POT1.PIN1, R1.pin_0
  N3: Part1.GND, S2.Pin_1, S2.Pin_2, POT1.PIN3, R2.Pin_1
  N4: Part1.A0, POT1.PIN2
  N5: Part1.A1, R1.pin_1, R2.Pin_0
